# Fritzing sketch e-home (saved by Fritzing 1.0.1rc)
breadboards: 1

parts:
  U1 = ESP32S-HiLetgo [part_number=ESP32S]
  A1 = Waveshare 1.54in epaper display
  DS18B1 = DS18B20 1-Wire Temperature Sensor Module [part_number=DS18B20]
  U2 = SIP - 8 pins [chip_label=IC package="SIP (Single Inline) [THT]"]
  R1 = Resistor [tolerance=±5% power=0.25 resistance=4.5k package=THT]
  Power_plug1 = Power plug

nets:
  3.3V: U1.3.3, A1.Pin_8, DS18B1.VDD, U2.VCC, R1.Pin_0, Power_plug1.VCC
  N1: U1.GPIO32, U2.SCL
  N2: U1.GPIO33, U2.SDA
  N3: U1.GPIO25, DS18B1.OUT, R1.Pin_1
  GND: U1.GND, A1.Pin_7, DS18B1.GND, U2.GND, U2.WAK, Power_plug1.GND
  N4: U1.GPIO4, A1.Pin_1
  N5: U1.GPIO5, A1.Pin_4
  N6: U1.GPIO18, A1.Pin_5
  N7: U1.GPIO21, A1.Pin_2
  N8: U1.GPIO22, A1.Pin_3
  N9: U1.GPIO23, A1.Pin_6

custom parts:
  ESP32S-HiLetgo: HiLetgo ESP-WROOM-32 ESP32 ESP-32S Development Board 2.4GHz Dual-Mode WiFi + Bluetooth Dual Cores Microcontroller The ESP32 integrated with Antenna switches, RF Balun, power amplifiers, low-noise amplifiers, filters, and management modules, and the entire solution occupies the least area of PCB. 2.4 GHz Wi-Fi plus Bluetooth dual-mode chip, with TSMC Ultra-low power consumption 40nm technology,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
  Waveshare 1.54in epaper display: This is an E-Ink display module, 1.54inch, 200x200 resolution, with embedded controller, communicating via SPI interface.
  DS18B20 1-Wire Temperature Sensor Module: DS18B20 1-Wire Temperature Sensor Module The DS18B20 digital thermometer provides 9-bit to 12-bit Celsius temperature measurements and has an alarm function with nonvolatile user-programmable upper and lower trigger points. The DS18B20 communicates over a 1-Wire bus that by definition requires only one data line (and ground) for communication with a central microprocessor. In addition, the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
  SIP - 8 pins: A SIP stand-in part for whatever you want. With 8 pins on a 300 mil single inline package (SIP) footprint.
